// Logisim project CO_Project.circ as structural Verilog: 19 circuits, main circuit main
module main (
);

  wire clock_1_out;

  Clock clock_1 (.out(clock_1_out));
  DataUnit dataunit_1 (.CLK(clock_1_out));  // open: in_8, in_34, in_35, in_36, in_37, in_38, in_39, in_40, in_9, in_41, in_42, in_43, in_10, in_11, in_12, in_4, in_13, in_14, in_15, in_16, in_17, in_18, in_3, in_19, in_2, in_5, in_20, in_21, in_22, in_23, in_24, in_25, in_26, in_27, in_6, in_28, in_29, in_30, in_31, in_7, in_32, in_33, out_44, out_45, out_46
endmodule

module DataUnit (
  input  CLK,
  input  [10:0] in_2,
  input  [3:0] in_3,
  input  in_4,
  input  in_5,
  input  in_6,
  input  in_7,
  input  in_8,
  input  in_9,
  input  in_10,
  input  in_11,
  input  in_12,
  input  in_13,
  input  in_14,
  input  in_15,
  input  in_16,
  input  in_17,
  input  in_18,
  input  in_19,
  input  in_20,
  input  in_21,
  input  in_22,
  input  in_23,
  input  in_24,
  input  in_25,
  input  in_26,
  input  in_27,
  input  in_28,
  input  in_29,
  input  in_30,
  input  in_31,
  input  in_32,
  input  in_33,
  input  in_34,
  input  in_35,
  input  in_36,
  input  in_37,
  input  in_38,
  input  in_39,
  input  in_40,
  input  in_41,
  input  in_42,
  input  in_43,
  output [7:0] out_44,
  output out_45,
  output out_46
);

  wire alu_1_e, alu_1_z, select_alu_1_en;
  wire [1:0] select_alu_1_s;
  wire [10:0] ar_register_1_out_8, undriven_8;
  wire [15:0] ac_register_1_q_out, alu_1_o, ar_register_1_q_out, dr_register_1_q_out, inpr_register_1_q_out,
       ir_register_1_q_out, memory_1_q, pc_register_1_q_out, undriven, undriven_2, undriven_3, undriven_4,
       undriven_5, undriven_6, undriven_7, undriven_9, undriven_10, undriven_11, undriven_12, undriven_13;

  AR_REGISTER ar_register_1 (
    .LD(in_4), .D_in(undriven), .CLK(CLK), .RESET(in_8), .AR_OUT(in_5), .CLR(in_7), .INC(in_6),
    .Q_Out(ar_register_1_q_out), .out_8(ar_register_1_out_8));
  PC_REGISTER pc_register_1 (
    .LD(in_9), .D_in(undriven_2), .CLK(CLK), .RESET(in_13), .PC_OUT(in_10), .CLR(in_12), .INC(in_11),
    .Q_Out(pc_register_1_q_out));
  IR_REGISTER ir_register_1 (
    .LD(in_14), .D_in(undriven_3), .CLK(CLK), .RESET(in_18), .LD_OUT(in_15), .CLR(in_17), .INC(in_16),
    .Q_OUT(ir_register_1_q_out), .out_8(in_2), .out_9(in_19), .out_11(in_3));
  AC_REGISTER ac_register_1 (
    .LD(in_20), .D_in(undriven_4), .CLK(CLK), .RESET(in_24), .AC_OUT(in_21), .CLR(in_23), .INC(in_22),
    .Q(undriven_5), .Q_OUT(ac_register_1_q_out));
  DR_REGISTER dr_register_1 (
    .LD(in_25), .D_in(undriven_6), .CLK(CLK), .RESET(in_29), .DR_OUT(in_26), .CLR(in_28), .Q(undriven_7),
    .INC(in_27), .Q_OUT(dr_register_1_q_out));
  ALU alu_1 (
    .in_5(in_34), .B(undriven_13), .A(undriven_12), .S(select_alu_1_s), .EN(select_alu_1_en), .O(alu_1_o),
    .E(alu_1_e), .Z(alu_1_z));
  FLAGS flags_1 (.E(alu_1_e), .Z(alu_1_z), .CLK(CLK), .in_2(in_33), .in_4(in_32), .out_6(out_46), .out_7(out_45));
  DATA_BUS data_bus_1 (
    .in_1(undriven_3), .in_3(inpr_register_1_q_out), .in_5(undriven_2), .in_7(dr_register_1_q_out),
    .in_9(ar_register_1_q_out), .in_11(undriven_4), .in_13(pc_register_1_q_out), .in_15(undriven_9),
    .in_17(undriven_5), .in_19(undriven_13), .in_21(ar_register_1_out_8), .in_18(undriven_12),
    .in_20(undriven_7), .in_22(undriven_8), .in_2(ir_register_1_q_out), .in_4(alu_1_o), .in_6(undriven_11),
    .in_8(undriven), .in_10(ac_register_1_q_out), .in_12(undriven_6), .in_14(undriven_10), .in_16(memory_1_q));
  INPR_REGISTER inpr_register_1 (
    .D_in(undriven_10), .LD(in_43), .CLK(CLK), .RESET(in_41), .AR_OUT(in_42), .Q_Out(inpr_register_1_q_out));
  OUTR_REGISTER outr_register_1 (.D_in(undriven_11), .LD(in_40), .CLK(CLK), .RESET(in_39), .Q_Out(out_44));
  MEMORY memory_1 (.O_E(in_31), .WE(in_30), .CLK(CLK), .D(undriven_9), .A(undriven_8), .Q(memory_1_q));
  SELECT_ALU select_alu_1 (
    .ADD(in_38), .AND(in_37), .CMA(in_36), .CLA(in_35), .EN(select_alu_1_en), .S(select_alu_1_s));

  // Notes on the sheet:
  //   DATA UNIT
endmodule

module ControlUnit (
  input  [3:0] D,
  input  EN_D,
  input  INC,
  input  [3:0] in_4,
  input  EN_INC,
  input  CLK,
  input  RESET_C
);

  wire instruction_decoder_1_d0, instruction_decoder_1_d1, instruction_decoder_1_d2,
       instruction_decoder_1_d3, instruction_decoder_1_d4, instruction_decoder_1_d5,
       instruction_decoder_1_d6, instruction_decoder_1_d7, instruction_decoder_1_d8,
       instruction_decoder_1_d9, instruction_decoder_1_d10, instruction_decoder_1_d11,
       instruction_decoder_1_d12, instruction_decoder_1_d13, instruction_decoder_1_d14,
       instruction_decoder_1_d15, timing_decoder_1_t0, timing_decoder_1_t1, timing_decoder_1_t2,
       timing_decoder_1_t3, timing_decoder_1_t4, timing_decoder_1_t5, timing_decoder_1_t6,
       timing_decoder_1_t7, timing_decoder_1_t8, timing_decoder_1_t9, timing_decoder_1_t10,
       timing_decoder_1_t11, timing_decoder_1_t12, timing_decoder_1_t13, timing_decoder_1_t14,
       timing_decoder_1_t15;
  wire [3:0] sequence_counter_1_o_p;

  Sequence_Counter sequence_counter_1 (
    .RESET(RESET_C), .EN_DATA(EN_D), .INC(INC), .EN_INC(EN_INC), .DATA_IN(D), .CLK(CLK),
    .O_P(sequence_counter_1_o_p));
  Timing_Decoder timing_decoder_1 (
    .SC(sequence_counter_1_o_p), .T0(timing_decoder_1_t0), .T15(timing_decoder_1_t15),
    .T1(timing_decoder_1_t1), .T14(timing_decoder_1_t14), .T2(timing_decoder_1_t2),
    .T13(timing_decoder_1_t13), .T3(timing_decoder_1_t3), .T12(timing_decoder_1_t12),
    .T4(timing_decoder_1_t4), .T11(timing_decoder_1_t11), .T5(timing_decoder_1_t5),
    .T10(timing_decoder_1_t10), .T6(timing_decoder_1_t6), .T9(timing_decoder_1_t9), .T7(timing_decoder_1_t7),
    .T8(timing_decoder_1_t8));
  Control_Logic control_logic_1 (
    .D0(instruction_decoder_1_d0), .D1(instruction_decoder_1_d1), .D2(instruction_decoder_1_d2),
    .D3(instruction_decoder_1_d3), .D4(instruction_decoder_1_d4), .D5(instruction_decoder_1_d5),
    .D6(instruction_decoder_1_d6), .D7(instruction_decoder_1_d7), .D8(instruction_decoder_1_d8),
    .D9(instruction_decoder_1_d9), .D10(instruction_decoder_1_d10), .D11(instruction_decoder_1_d11),
    .D12(instruction_decoder_1_d12), .D13(instruction_decoder_1_d13), .D14(instruction_decoder_1_d14),
    .D15(instruction_decoder_1_d15), .T0(timing_decoder_1_t0), .T1(timing_decoder_1_t1),
    .T2(timing_decoder_1_t2), .T3(timing_decoder_1_t3), .T4(timing_decoder_1_t4), .T5(timing_decoder_1_t5),
    .T6(timing_decoder_1_t6), .T7(timing_decoder_1_t7), .T8(timing_decoder_1_t8), .T9(timing_decoder_1_t9),
    .T10(timing_decoder_1_t10), .T11(timing_decoder_1_t11), .T12(timing_decoder_1_t12),
    .T13(timing_decoder_1_t13), .T14(timing_decoder_1_t14), .T15(timing_decoder_1_t15));
  Instruction_Decoder instruction_decoder_1 (
    .S(in_4), .D0(instruction_decoder_1_d0), .D15(instruction_decoder_1_d15), .D1(instruction_decoder_1_d1),
    .D14(instruction_decoder_1_d14), .D2(instruction_decoder_1_d2), .D13(instruction_decoder_1_d13),
    .D3(instruction_decoder_1_d3), .D12(instruction_decoder_1_d12), .D4(instruction_decoder_1_d4),
    .D11(instruction_decoder_1_d11), .D5(instruction_decoder_1_d5), .D10(instruction_decoder_1_d10),
    .D6(instruction_decoder_1_d6), .D9(instruction_decoder_1_d9), .D7(instruction_decoder_1_d7),
    .D8(instruction_decoder_1_d8));

  // Notes on the sheet:
  //   CONTROLL UNIT
endmodule

module DATA_BUS (
  input  [15:0] in_1,
  input  [15:0] in_2,
  input  [15:0] in_3,
  input  [15:0] in_4,
  input  [15:0] in_5,
  input  [15:0] in_6,
  input  [15:0] in_7,
  input  [15:0] in_8,
  input  [15:0] in_9,
  input  [15:0] in_10,
  input  [15:0] in_11,
  input  [15:0] in_12,
  input  [15:0] in_13,
  input  [15:0] in_14,
  input  [15:0] in_15,
  input  [15:0] in_16,
  input  [15:0] in_17,
  input  [15:0] in_18,
  input  [15:0] in_19,
  input  [15:0] in_20,
  input  [10:0] in_21,
  input  [10:0] in_22
);


  assign in_2 = in_1;
  assign in_3 = in_1;
  assign in_4 = in_1;
  assign in_5 = in_1;
  assign in_6 = in_1;
  assign in_7 = in_1;
  assign in_8 = in_1;
  assign in_9 = in_1;
  assign in_10 = in_1;
  assign in_11 = in_1;
  assign in_12 = in_1;
  assign in_13 = in_1;
  assign in_14 = in_1;
  assign in_15 = in_1;
  assign in_16 = in_1;
  assign in_18 = in_17;
  assign in_20 = in_19;
  assign in_22 = in_21;

  // Notes on the sheet:
  //   DATA BUS
endmodule

module ALU (
  input  [15:0] B,
  input  [15:0] A,
  input  EN,
  input  [1:0] S,
  input  in_5,
  output E,
  output Z,
  output [15:0] O
);

  wire or_1_out;
  wire [15:0] adder_1_out, and_1_out, multiplexer_1_out, not_1_out;

  Adder #(.width(16)) adder_1 (.a(A), .b(B), .out(adder_1_out), .cout(E));  // open: cin
  assign and_1_out = A & B;  // AND_Gate and_1, 16 bits wide
  assign not_1_out = ~A;  // NOT_Gate not_1, 16 bits wide
  Multiplexer #(.enable("true"), .select(2), .width(16)) multiplexer_1 (
    .in0(adder_1_out), .in1(and_1_out), .in2(not_1_out), .in3({16{1'b0}}), .out(multiplexer_1_out), .sel(S),
    .en(EN));
  or or_1 (or_1_out, multiplexer_1_out[0], multiplexer_1_out[1], multiplexer_1_out[2], multiplexer_1_out[3], multiplexer_1_out[4], multiplexer_1_out[5], multiplexer_1_out[6], multiplexer_1_out[7], multiplexer_1_out[9], multiplexer_1_out[10], multiplexer_1_out[11], multiplexer_1_out[12], multiplexer_1_out[13], multiplexer_1_out[14], multiplexer_1_out[15]);
  assign O = in_5 ? multiplexer_1_out : 16'bz;  // Controlled_Buffer controlled_buffer_1
  not not_2 (Z, or_1_out);
endmodule

module FLAGS (
  input  E,
  input  in_2,
  input  Z,
  input  in_4,
  input  CLK,
  output out_6,
  output out_7
);

  D_Flip_Flop d_ff_1 (.D(E), .clk(CLK), .Q(out_6), .reset(in_2));  // open: Qn, preset
  D_Flip_Flop d_ff_2 (.D(Z), .clk(CLK), .Q(out_7), .reset(in_4));  // open: Qn, preset
endmodule

module AR_REGISTER (
  input  AR_OUT,
  input  [15:0] D_in,
  input  CLK,
  input  RESET,
  input  LD,
  input  CLR,
  input  INC,
  output [10:0] out_8,
  output [15:0] Q_Out
);

  wire not_1_out, or_1_out;
  wire [0:0] and_1_out;
  wire [10:0] adder_1_out, multiplexer_1_out;
  wire [15:0] bit_extender_1_out;

  or or_1 (or_1_out, LD, INC, CLR);
  Register #(.width(11)) register_1 (.D(multiplexer_1_out), .en(or_1_out), .clk(CLK), .Q(out_8), .clr(RESET));
  Adder #(.width(11)) adder_1 (.a(out_8), .b(11'h1), .out(adder_1_out));  // open: cin, cout
  assign bit_extender_1_out = {{5{1'b0}}, out_8};  // Bit_Extender bit_extender_1
  assign Q_Out = AR_OUT ? bit_extender_1_out : 16'bz;  // Controlled_Buffer controlled_buffer_1
  Multiplexer #(.select(2), .width(11)) multiplexer_1 (
    .in0(D_in[10:0]), .in1(adder_1_out), .in2({11{1'b0}}), .out(multiplexer_1_out), .sel({CLR, and_1_out[0]}));  // open: in3
  and and_1 (and_1_out[0], not_1_out, INC);
  not not_1 (not_1_out, CLR);
endmodule

module DR_REGISTER (
  input  [15:0] Q,
  input  DR_OUT,
  input  [15:0] D_in,
  input  CLK,
  input  RESET,
  input  CLR,
  input  INC,
  input  LD,
  output [15:0] Q_OUT
);

  wire not_1_out, or_1_out;
  wire [0:0] and_1_out;
  wire [15:0] adder_1_out, multiplexer_1_out;

  or or_1 (or_1_out, LD, INC, CLR);
  Register #(.width(16)) register_1 (.D(multiplexer_1_out), .en(or_1_out), .clk(CLK), .Q(Q), .clr(RESET));
  assign Q_OUT = DR_OUT ? Q : 16'bz;  // Controlled_Buffer controlled_buffer_1
  Adder #(.width(16)) adder_1 (.a(Q), .b(16'h1), .out(adder_1_out));  // open: cin, cout
  Multiplexer #(.select(2), .width(16)) multiplexer_1 (
    .in0(D_in), .in1(adder_1_out), .in2({16{1'b0}}), .out(multiplexer_1_out), .sel({CLR, and_1_out[0]}));  // open: in3
  and and_1 (and_1_out[0], not_1_out, INC);
  not not_1 (not_1_out, CLR);
endmodule

module IR_REGISTER (
  input  LD_OUT,
  input  [15:0] D_in,
  input  CLK,
  input  RESET,
  input  CLR,
  input  INC,
  input  LD,
  output [10:0] out_8,
  output out_9,
  output [15:0] Q_OUT,
  output [3:0] out_11
);

  wire not_1_out, or_1_out;
  wire [0:0] and_1_out;
  wire [15:0] adder_1_out, multiplexer_1_out;

  or or_1 (or_1_out, LD, INC, CLR);
  Register #(.width(16)) register_1 (
    .D(multiplexer_1_out), .en(or_1_out), .clk(CLK), .Q({out_11, out_9, out_8}), .clr(RESET));
  assign Q_OUT = LD_OUT ? {out_11, out_9, out_8} : 16'bz;  // Controlled_Buffer controlled_buffer_1
  Adder #(.width(16)) adder_1 (.a({out_11, out_9, out_8}), .b(16'h1), .out(adder_1_out));  // open: cin, cout
  Multiplexer #(.select(2), .width(16)) multiplexer_1 (
    .in0(D_in), .in1(adder_1_out), .in2({16{1'b0}}), .out(multiplexer_1_out), .sel({CLR, and_1_out[0]}));  // open: in3
  and and_1 (and_1_out[0], not_1_out, INC);
  not not_1 (not_1_out, CLR);
endmodule

module INPR_REGISTER (
  input  [15:0] D_in,
  input  AR_OUT,
  input  LD,
  input  CLK,
  input  RESET,
  output [15:0] Q_Out
);

  wire [7:0] register_1_q;
  wire [15:0] bit_extender_1_out;

  Register register_1 (.D(D_in[7:0]), .en(LD), .clk(CLK), .Q(register_1_q), .clr(RESET));
  assign bit_extender_1_out = {{8{1'b0}}, register_1_q};  // Bit_Extender bit_extender_1
  assign Q_Out = AR_OUT ? bit_extender_1_out : 16'bz;  // Controlled_Buffer controlled_buffer_1
endmodule

module OUTR_REGISTER (
  input  [15:0] D_in,
  input  LD,
  input  CLK,
  input  RESET,
  output [7:0] Q_Out
);

  Register register_1 (.D(D_in[7:0]), .en(LD), .clk(CLK), .Q(Q_Out), .clr(RESET));
endmodule

module PC_REGISTER (
  input  PC_OUT,
  input  [15:0] D_in,
  input  CLK,
  input  RESET,
  input  LD,
  input  CLR,
  input  INC,
  output [15:0] Q_Out
);

  wire not_1_out, or_1_out;
  wire [0:0] and_1_out;
  wire [10:0] adder_1_out, multiplexer_1_out, register_1_q;
  wire [15:0] bit_extender_1_out;

  or or_1 (or_1_out, LD, INC, CLR);
  Register #(.width(11)) register_1 (.D(multiplexer_1_out), .en(or_1_out), .clk(CLK), .Q(register_1_q), .clr(RESET));
  Adder #(.width(11)) adder_1 (.a(register_1_q), .b(11'h1), .out(adder_1_out));  // open: cin, cout
  assign bit_extender_1_out = {{5{1'b0}}, register_1_q};  // Bit_Extender bit_extender_1
  assign Q_Out = PC_OUT ? bit_extender_1_out : 16'bz;  // Controlled_Buffer controlled_buffer_1
  Multiplexer #(.select(2), .width(11)) multiplexer_1 (
    .in0(D_in[10:0]), .in1(adder_1_out), .in2({11{1'b0}}), .out(multiplexer_1_out), .sel({CLR, and_1_out[0]}));  // open: in3
  and and_1 (and_1_out[0], not_1_out, INC);
  not not_1 (not_1_out, CLR);
endmodule

module AC_REGISTER (
  input  [15:0] Q,
  input  AC_OUT,
  input  [15:0] D_in,
  input  CLK,
  input  RESET,
  input  CLR,
  input  INC,
  input  LD,
  output [15:0] Q_OUT
);

  wire not_1_out, or_1_out;
  wire [0:0] and_1_out;
  wire [15:0] adder_1_out, multiplexer_1_out;

  or or_1 (or_1_out, LD, INC, CLR);
  Register #(.width(16)) register_1 (.D(multiplexer_1_out), .en(or_1_out), .clk(CLK), .Q(Q), .clr(RESET));
  assign Q_OUT = AC_OUT ? Q : 16'bz;  // Controlled_Buffer controlled_buffer_1
  Adder #(.width(16)) adder_1 (.a(Q), .b(16'h1), .out(adder_1_out));  // open: cin, cout
  Multiplexer #(.select(2), .width(16)) multiplexer_1 (
    .in0(D_in), .in1(adder_1_out), .in2({16{1'b0}}), .out(multiplexer_1_out), .sel({CLR, and_1_out[0]}));  // open: in3
  and and_1 (and_1_out[0], not_1_out, INC);
  not not_1 (not_1_out, CLR);
endmodule

module MEMORY (
  input  WE,
  input  [10:0] A,
  input  O_E,
  input  CLK,
  input  [15:0] D,
  output [15:0] Q
);

  RAM #(.addrWidth(10), .dataWidth(16)) ram_1 (.addr(A[9:0]), .we(WE), .oe(O_E), .clk(CLK), .din(D), .dout(Q));
endmodule

module SELECT_ALU (
  input  ADD,
  input  AND,
  input  CMA,
  input  CLA,
  output EN,
  output [1:0] S
);

  wire [0:0] not_4_out;
  wire [1:0] not_1_out;
  wire [1:1] not_3_out;

  NotExactlyOne xnor_1[1:0] (
    .out(S), .in0(not_1_out), .in1({not_3_out[1], AND}), .in2({CMA, not_4_out[0]}), .in3({2{CLA}}));
  or or_1 (EN, ADD, AND, CMA, CLA);
  not not_1 (not_1_out[0], ADD);
  not not_2 (not_1_out[1], ADD);
  not not_3 (not_3_out[1], AND);
  not not_4 (not_4_out[0], CMA);
endmodule

module Sequence_Counter (
  input  RESET,
  input  EN_DATA,
  input  INC,
  input  EN_INC,
  input  CLK,
  input  [3:0] DATA_IN,
  output [3:0] O_P
);

  Counter #(.max('hf), .width(4)) counter_1 (
    .clr(RESET), .load(EN_DATA), .up(INC), .count(EN_INC), .clk(CLK), .D(DATA_IN), .Q(O_P));  // open: carry
endmodule

module Timing_Decoder (
  input  [3:0] SC,
  output T0,
  output T1,
  output T2,
  output T3,
  output T4,
  output T5,
  output T6,
  output T7,
  output T15,
  output T14,
  output T13,
  output T12,
  output T11,
  output T10,
  output T9,
  output T8
);

  Decoder #(.select(4)) decoder_1 (
    .out0(T0), .out1(T1), .out2(T2), .out3(T3), .out4(T4), .out5(T5), .out6(T6), .out7(T7), .out8(T8),
    .out9(T9), .out10(T10), .out11(T11), .out12(T12), .out13(T13), .out14(T14), .out15(T15), .sel(SC));  // open: en
endmodule

module Instruction_Decoder (
  input  [3:0] S,
  output D0,
  output D1,
  output D2,
  output D3,
  output D4,
  output D5,
  output D6,
  output D7,
  output D15,
  output D14,
  output D13,
  output D12,
  output D11,
  output D10,
  output D9,
  output D8
);

  Decoder #(.select(4)) decoder_1 (
    .out0(D0), .out1(D1), .out2(D2), .out3(D3), .out4(D4), .out5(D5), .out6(D6), .out7(D7), .out8(D8),
    .out9(D9), .out10(D10), .out11(D11), .out12(D12), .out13(D13), .out14(D14), .out15(D15), .sel(S));  // open: en
endmodule

module Control_Logic (
  input  T0,
  input  D0,
  input  T1,
  input  D1,
  input  T2,
  input  D2,
  input  T3,
  input  D3,
  input  T4,
  input  D4,
  input  T5,
  input  D5,
  input  T6,
  input  D6,
  input  T7,
  input  D7,
  input  T8,
  input  D8,
  input  T9,
  input  D9,
  input  T10,
  input  D10,
  input  T11,
  input  D11,
  input  T12,
  input  D12,
  input  T13,
  input  D13,
  input  T14,
  input  D14,
  input  T15,
  input  D15
);
endmodule
